# Fritzing sketch AA-Robot_MotorControlBoard (saved by Fritzing 0.9.3b)
stripboards: 1

parts:
  DIP-Relay1 = DIP-Relay-D31A [part_number=D31A*]
  1 = female pin header, 2 pins [form="♀ (female)"]
  DIP-Relay2 = DIP-Relay-D31A [part_number=D31A*]
  DIP-Relay3 = DIP-Relay-D31A [part_number=D31A*]
  6 = female pin header, 2 pins [form="♀ (female)"]
  7 = female pin header, 2 pins [form="♀ (female)"]
  5 = female pin header, 2 pins [form="♀ (female)"]
  4 = female pin header, 2 pins [form="♀ (female)"]
  2 = female pin header, 2 pins [form="♀ (female)"]
  3 = female pin header, 2 pins [form="♀ (female)"]

nets:
  N1: DIP-Relay1.A1_Switch_Terminal_A, 3.pin1, 3.pin2
  N2: DIP-Relay1.B1_Switch_Terminal_B, DIP-Relay2.B2_Switch_Terminal_B, 7.pin1, 7.pin2
  N3: DIP-Relay1.B2_Switch_Terminal_B, DIP-Relay2.B1_Switch_Terminal_B, 6.pin1, 6.pin2
  N4: DIP-Relay1.Coil_Sheeld, DIP-Relay2.Coil_Sheeld, 5.pin1, 5.pin2
  N5: DIP-Relay1.n.c., 1.pin1, 1.pin2, DIP-Relay2.n.c., DIP-Relay3.n.c.
  N6: DIP-Relay1.A2_Switch_Terminal_A, DIP-Relay3.A1_Switch_Terminal_A, 2.pin1, 2.pin2
  N7: DIP-Relay2.A1_Switch_Terminal_A, DIP-Relay3.B1_Switch_Terminal_B
  N8: DIP-Relay3.Coil_Sheeld, 4.pin1, 4.pin2

notes:
  1 - ARD_GND
  2 - BAT_IN
  3 - BAT_OUT
  4 - PWR_CTRL
  5 - DRCTN_CTRL
  6 - MOTR+
  7 - MOTR-
